# Fritzing sketch ar06_R (saved by Fritzing 0.9.3b)
breadboards: 1

parts:
  부품1 = Arduino Uno (Rev3)
  R1 = Resistor [tolerance=±5% resistance=1k package=THT]

nets:
  N1: 부품1.5V, R1.Pin_0
  N2: 부품1.GND, R1.Pin_1
