# Fritzing sketch AR06_4led (saved by Fritzing 0.9.3b)
breadboards: 1

parts:
  R1 = Resistor [tolerance=±5% resistance=220 package=THT]
  R2 = Resistor [tolerance=±5% resistance=220 package=THT]
  LED1 = LED - 5mm [color="Green (560nm)" package="5 mm [THT]"]
  LED2 = LED - 5mm [color="Red (633nm)" package="5 mm [THT]"]
  부품1 = Arduino Uno (Rev3)
  LED3 = LED - 5mm [color="Yellow (592nm)" package="5 mm [THT]"]
  LED4 = LED - 5mm [color="Blue (470nm)" package="5 mm [THT]"]
  R4 = Resistor [tolerance=±5% resistance=220 package=THT]
  R5 = Resistor [tolerance=±5% resistance=220 package=THT]

nets:
  N1: R1.Pin_0, LED1.cathode
  N2: R1.Pin_1, R2.Pin_1, 부품1.GND, R4.Pin_1, R5.Pin_1
  N3: R2.Pin_0, LED2.cathode
  N4: LED1.anode, 부품1.D5_PWM
  N5: LED2.anode, 부품1.D3_PWM
  N6: 부품1.D9_PWM, LED3.anode
  N7: 부품1.D6_PWM, LED4.anode
  N8: LED3.cathode, R5.Pin_0
  N9: LED4.cathode, R4.Pin_0
