# Fritzing sketch cds_I2C_LCD (saved by Fritzing 0.9.3b)
breadboards: 1

parts:
  부품1 = Arduino Uno (Rev3)
  R1 = Resistor [tolerance=±5% resistance=1k package=THT]
  Display1 = LCD screen 16x2 IIC [part_number=101290]
  R2 = Photocell (LDR) [package=THT]

nets:
  N1: 부품1.A0, R1.Pin_0, R2.pin_1
  N2: 부품1.A4/SDA, Display1.SDA
  N3: 부품1.A5/SCL, Display1.SCL
  GND: 부품1.GND, Display1.GND, R2.pin_0
  5V: 부품1.5V, R1.Pin_1, Display1.VCC

custom parts:
  LCD screen 16x2 IIC: LCD screen with HD44780 controller enables showing text, symbols, value or anything else that comes from Croduino/Arduino. It is capable of showing 16 symbols in two lines and therefore can be used in many projects that need to send clearly visible and legible output information.. • Color of symbols: White • Backlight: Blue • Dimensions: 80 x 36 x 12 mm • Screen dimensions: 64.5 x 16 mm •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
