# Fritzing sketch CdS_TMP36_LCD (saved by Fritzing 0.9.3b)
breadboards: 1

parts:
  R2 = Photocell (LDR) [package=THT]
  R3 = Resistor [tolerance=±5% resistance=10k package=THT]
  부품1 = Arduino Uno (Rev3)
  Display1 = LCD screen 16x2 IIC [part_number=101290]
  T1 = TMP36 Temperature Sensor [package="TO92 [THT]"]

nets:
  GND: R2.pin_0, 부품1.GND, Display1.GND, T1.GND
  N1: R2.pin_1, R3.Pin_0, 부품1.A1
  5V: R3.Pin_1, 부품1.5V, Display1.VCC, T1.+Vs
  N2: 부품1.A0, T1.Vout
  N3: 부품1.A4/SDA, Display1.SDA
  N4: 부품1.A5/SCL, Display1.SCL

custom parts:
  LCD screen 16x2 IIC: LCD screen with HD44780 controller enables showing text, symbols, value or anything else that comes from Croduino/Arduino. It is capable of showing 16 symbols in two lines and therefore can be used in many projects that need to send clearly visible and legible output information.. • Color of symbols: White • Backlight: Blue • Dimensions: 80 x 36 x 12 mm • Screen dimensions: 64.5 x 16 mm •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
